# Fritzing sketch Scheme (saved by Fritzing 0.9.3b)

parts:
  Raspberry_Pi_1 = Raspberry Pi 3 [part_number=RPI-3-V1.2]
  Q1 = TRANSISTOR_NPN [part_number=2N3904 package=to-92]
  R1 = Resistor [tolerance=±5% resistance=100 package="0402 [SMD]"]
  S1 = Pushbutton [package="[THT]"]
  R2 = Resistor [tolerance=±5% resistance=500 package="0603 [SMD]"]
  M1 = DC Motor

nets:
  N1: Raspberry_Pi_1.GND, Q1.E, S1.Pin_2
  N2: Raspberry_Pi_1.GIPO12, R2.Pin_1
  N3: Raspberry_Pi_1.GIPO14, R1.Pin_1
  N4: Raspberry_Pi_1.5V, M1.pin_1
  N5: Q1.B, R1.Pin_0
  N6: Q1.C, M1.pin_2
  N7: S1.Pin_4, R2.Pin_0

notes:
  c
  b
  e
  +
  -
